# Fritzing sketch Motorcycle Computer (saved by Fritzing 0.9.2b)
breadboards: 1

parts:
  GPS1 = Adafruit Ultimate GPS Breakout
  Part2 = Photon
  VCC1 = Battery
  microSD1 = MicroSD Breakout

nets:
  N1: GPS1.TX, Part2.RX
  N2: GPS1.RX, Part2.TX
  GND: GPS1.GND, VCC1.-, microSD1.GND
  VIN: GPS1.VIN, Part2.VIN, VCC1.+
  N3: Part2.A2, microSD1.CS
  N4: Part2.A3, microSD1.CLK
  N5: Part2.A4, microSD1.DO
  N6: Part2.A5, microSD1.DI
  N7: Part2.3V3, microSD1.3v

notes:
  5V power Source

custom parts:
  MicroSD Breakout: 5V-ready microSD Breakout with Level Shifter
